// Logisim project PA1.circ as structural Verilog: 7 circuits, main circuit main
module main (
  input  Reset,
  input  Clock_Input
);

  wire [1:0] register_1_q;
  wire [4:0] _15_11_q, _20_16_q;
  wire [5:0] _31_26_q;
  wire [29:0] incrementer_1_p2, register_1_q_2;
  wire [31:0] bit_extender_1_out, mipsprogramrom_1_p1, register_2_q, registerfile_1_p3, registerfile_1_p4,
       registerfile_1_p6, registerfile_1_p7, registerfile_1_p8;

  Register #(.width(32)) register_1 (
    .D({incrementer_1_p2, register_1_q}), .Q({register_1_q_2, register_1_q}), .clk(Clock_Input), .clr(Reset));  // open: en
  // Incrementer incrementer_1: pin names not known; wires that end beside it: register_1_q_2, incrementer_1_p2, {register_1_q_2, register_1_q}
  // MIPSProgramROM mipsprogramrom_1: pin names not known; wires that end beside it: mipsprogramrom_1_p1, Clock_Input
  Register #(.width(32)) register_2 (.D(mipsprogramrom_1_p1), .Q(register_2_q), .clk(Clock_Input));  // open: en, clr
  // RegisterFile registerfile_1: pin names not known; wires that end beside it: register_2_q[25:21], register_2_q[20:16], registerfile_1_p3, registerfile_1_p4, Clock_Input, registerfile_1_p6, registerfile_1_p7, registerfile_1_p8
  assign bit_extender_1_out = {{16{1'b0}}, register_2_q[15:0]};  // Bit_Extender bit_extender_1
  Register #(.width(32)) A (.D(registerfile_1_p3), .Q(registerfile_1_p6), .clk(Clock_Input));  // open: en, clr
  Register #(.width(32)) B (.D(registerfile_1_p4), .Q(registerfile_1_p7), .clk(Clock_Input));  // open: en, clr
  Register #(.width(32)) _15_0 (.D(bit_extender_1_out), .Q(registerfile_1_p8), .clk(Clock_Input));  // open: en, clr
  Register #(.width(5)) _15_11 (.D(register_2_q[15:11]), .Q(_15_11_q), .clk(Clock_Input));  // open: en, clr
  Register #(.width(5)) _20_16 (.D(register_2_q[20:16]), .Q(_20_16_q), .clk(Clock_Input));  // open: en, clr
  Register #(.width(6)) _31_26 (.D(register_2_q[31:26]), .Q(_31_26_q), .clk(Clock_Input));  // open: en, clr

  // Other names for the same wires on the sheet: C = Clock_Input
endmodule

module R_Type (
  input  [31:0] in_1,
  output [3:0] OP,
  output Var_Shift,
  output SLT,
  output MOV,
  output MOV_Z_N,
  output [4:0] H_Shift
);

  wire and_1_out, and_3_out, not_1_out;
  wire [3:0] multiplexer_1_out, multiplexer_2_out;

  and and_1 (and_1_out, in_1[1], ~in_1[2], in_1[3]);  // AND_Gate
  Multiplexer #(.width(4), .enable("false")) multiplexer_1 (
    .in0({1'b0, in_1[1:0], 1'b0}), .in1(4'b0110), .out(multiplexer_1_out), .sel(in_1[0]));
  Multiplexer #(.width(4), .enable("false")) multiplexer_2 (
    .in0({in_1[2:0], 1'b0}), .in1(4'b0110), .out(multiplexer_2_out), .sel(and_1_out));
  and and_2 (MOV, and_1_out, ~in_1[5]);  // AND_Gate
  not not_1 (not_1_out, and_3_out);
  and and_3 (and_3_out, ~in_1[3], ~in_1[4], ~in_1[5]);  // AND_Gate
  and and_4 (SLT, and_1_out, ~MOV);  // AND_Gate
  Multiplexer #(.width(4), .enable("false")) multiplexer_3 (
    .in0(multiplexer_1_out), .in1(multiplexer_2_out), .out(OP), .sel(not_1_out));
  and and_5 (Var_Shift, and_3_out, in_1[2]);

  assign H_Shift = in_1[10:6];
  assign MOV_Z_N = in_1[4];
endmodule

module RI_Type (
  input  [31:0] in_1,
  output [3:0] OpCode,
  output SLT,
  output LUI
);

  wire [3:0] multiplexer_1_out;

  and and_1 (SLT, in_1[27], ~in_1[28]);  // AND_Gate
  and and_2 (LUI, in_1[26], in_1[27], in_1[28]);
  Multiplexer #(.width(4), .enable("false")) multiplexer_1 (
    .in0({in_1[28:26], 1'b0}), .in1(4'b0110), .out(multiplexer_1_out), .sel(SLT));
  Multiplexer #(.width(4), .enable("false")) multiplexer_2 (
    .in0(multiplexer_1_out), .in1(4'b0000), .out(OpCode), .sel(LUI));
endmodule

module IB_Type (
  input  [31:0] in_1,
  output [3:0] OpCode
);


  assign OpCode = 4'b0000;
endmodule

module PC (
  input  Reset,
  input  Clock_Input,
  output [31:0] Op
);

  wire [29:0] incrementer_1_p2;
  wire [31:0] register_1_q;

  Register #(.width(32)) register_1 (
    .D({incrementer_1_p2, register_1_q[1:0]}), .Q(register_1_q), .clk(Clock_Input), .clr(Reset));  // open: en
  // Incrementer incrementer_1: pin names not known; wires that end beside it: register_1_q[31:2], incrementer_1_p2, register_1_q
  // MIPSProgramROM mipsprogramrom_1: pin names not known; wires that end beside it: Op
endmodule

module Control (
  input  [31:0] in_1,
  output Var_Shift,
  output MOV,
  output MOV_Z_N,
  output SLT,
  output LUI,
  output [4:0] H,
  output [3:0] OP,
  output Imm,
  output No_WB
);

  wire and_1_out, and_2_out, and_3_out, and_5_out, r_type_1_p4, ri_type_1_p3;
  wire [3:0] ib_type_1_opcode, j_type_1_opcode, multiplexer_1_out, multiplexer_3_out, r_type_1_p2,
       ri_type_1_p2;

  J_Type j_type_1 (.in_1(in_1), .OpCode(j_type_1_opcode));
  // R_Type r_type_1: pin names not known; wires that end beside it: in_1, r_type_1_p2, Var_Shift, r_type_1_p4, MOV, MOV_Z_N, H
  and and_1 (and_1_out, ~in_1[26], ~in_1[27], ~in_1[28], ~in_1[29], ~in_1[30], ~in_1[31]);  // AND_Gate
  // RI_Type ri_type_1: pin names not known; wires that end beside it: in_1, ri_type_1_p2, ri_type_1_p3, LUI
  IB_Type ib_type_1 (.in_1(in_1), .OpCode(ib_type_1_opcode));
  and and_2 (and_2_out, in_1[26], ~in_1[27], ~in_1[28], ~in_1[29], ~in_1[30], ~in_1[31]);  // AND_Gate
  and and_3 (and_3_out, in_1[27], ~in_1[28], ~in_1[29], ~in_1[30], ~in_1[31]);  // AND_Gate
  Multiplexer #(.width(4), .enable("false")) multiplexer_1 (
    .in0(ib_type_1_opcode), .in1(j_type_1_opcode), .out(multiplexer_1_out), .sel(and_2_out));
  Multiplexer #(.width(4), .enable("false")) multiplexer_2 (
    .in0(multiplexer_3_out), .in1(r_type_1_p2), .out(OP), .sel(and_1_out));
  Multiplexer #(.width(4), .enable("false")) multiplexer_3 (
    .in0(ri_type_1_p2), .in1(multiplexer_1_out), .out(multiplexer_3_out), .sel(and_3_out));
  or or_1 (SLT, r_type_1_p4, ri_type_1_p3);
  and and_4 (Imm, ~and_1_out, ~and_3_out, ~and_2_out);  // AND_Gate
  and and_5 (and_5_out, ~and_1_out, and_3_out, ~and_2_out);  // AND_Gate
  or or_2 (No_WB, and_2_out, and_5_out);
endmodule

module J_Type (
  input  [31:0] in_1,
  output [3:0] OpCode
);


  assign OpCode = 4'b0000;
endmodule
