// Logisim project project1.circ as structural Verilog
module Decode (
  input  [31:0] Op,
  output whichSa,
  output WriteEn,
  output [4:0] Rs,
  output [4:0] Rt,
  output [3:0] ALU_Op,
  output [4:0] Rd,
  output B_or_Immediate,
  output [31:0] Immediate,
  output Is_R,
  output Mem
);

  Non_Immediate_Decode non_immediate_decode_1 (
    .Op(Op), .Memory(Mem), .whichSA(whichSa), .Enable(WriteEn), .rd(Rd), .rt(Rt), .rs(Rs), .Control(ALU_Op),
    .IsR(Is_R));
  Immediate_Decode immediate_decode_1 (.IsR(Is_R), .Op(Op), .BorImmediate(B_or_Immediate), .Immediate(Immediate));
endmodule

module _4 (
  input  [31:0] in_1,
  output [31:0] out_2
);

  // Incrementer incrementer_1: pin names not known; wires that end beside it: in_1[31:2], out_2[31:2]

  assign out_2[1:0] = in_1[1:0];
endmodule

module Fetch (
  input  Clock,
  output [31:0] RomIn,
  output [31:0] PC___4
);

  Register #(.width(32)) register_1 (.D(PC___4), .Q(RomIn), .clk(Clock));  // open: en, clr
  _4 u_4_1 (.in_1(RomIn), .out_2(PC___4));
endmodule

module MIPS32 (
  input  Clock
);

  wire BorI, Decode_b_or_immediate, Decode_is_r, Decode_mem, Decode_whichsa, Decode_writeen, Ex_MEM_mem_2,
       Ex_Mem_WE, Execute_mem_out, ID_EX_mem_2, Is_R, Mem, Memory_mem_out, Memory_we_2, We, we_t, wEn, WhSa,
       write;
  wire [3:0] Decode_alu_op, Op;
  wire [4:0] Decode_rd, Dest, dest_t, Ex_Mem_Rd, Memory_dest_2, RD, Rd_t, Rs, rS_t, Rt, rT_t;
  wire [31:0] A, B, D, d_t, Decode_immediate, Ex_MEM_d_2, Execute_target, Fetch_pc___4, Fetch_romin,
       ID_EX_pc_4_2, IF_ID_instr, IF_ID_pc_4_2, Imm, m, Mem_D, MEM_WB_d_2, Memory_m, mipsprogramrom_1_p2,
       regA, regB;

  Fetch Fetch (.RomIn(Fetch_romin), .Clock(Clock), .PC___4(Fetch_pc___4));
  // MIPSProgramROM mipsprogramrom_1: pin names not known; wires that end beside it: Fetch_romin, mipsprogramrom_1_p2, Clock, write
  IF_DE IF_ID (
    .InstrIn(mipsprogramrom_1_p2), .PC_4(Fetch_pc___4), .clk(Clock), .Instr(IF_ID_instr),
    .PC_4_2(IF_ID_pc_4_2));
  // Probe on D
  Decode Decode (
    .Op(IF_ID_instr), .whichSa(Decode_whichsa), .WriteEn(Decode_writeen), .Rs(rS_t), .Rt(rT_t),
    .ALU_Op(Decode_alu_op), .Rd(Decode_rd), .B_or_Immediate(Decode_b_or_immediate),
    .Immediate(Decode_immediate), .Is_R(Decode_is_r), .Mem(Decode_mem));
  // Probe on RD
  // RegisterFile registerfile_1: pin names not known; wires that end beside it: D, RD, rS_t, rT_t, regA, regB
  ID_EX ID_EX (
    .A(regA), .B(regB), .WE(Decode_writeen), .Rt(rT_t), .Op(Decode_alu_op), .Rd(Decode_rd),
    .B_or_Immediate(Decode_b_or_immediate), .Imm(Decode_immediate), .isR(Decode_is_r), .Mem(Decode_mem),
    .PC_4(IF_ID_pc_4_2), .whichSA(Decode_whichsa), .A_2(A), .B_2(B), .WE_2(We), .Rt_2(Rt), .Op_2(Op),
    .Rd_2(Rd_t), .B_or_Imm(BorI), .Imm_2(Imm), .is_R(Is_R), .Mem_2(ID_EX_mem_2), .PC_4_2(ID_EX_pc_4_2),
    .whichSA_2(WhSa), .clk(Clock), .Rs(rS_t), .Rs_2(Rs));
  // Probe on We
  // Probe on Imm
  // Probe on BorI
  Execute Execute (
    .Rt(Rt), .A(A), .Rd(Rd_t), .Is_R(Is_R), .Mem_D(Mem_D), .WB_D(D), .ALU_Op(Op), .Immediate(Imm), .B(B),
    .whichSA(WhSa), .WE(We), .Ex_Mem_WE(Ex_Mem_WE), .Ex_Mem_Rd(Ex_Mem_Rd), .B_or_Immediate(BorI),
    .Mem_WB_WE(we_t), .Mem_WB_Rd(Dest), .Mem_in(ID_EX_mem_2), .PC_4(ID_EX_pc_4_2), .ID_Ex_Ra(Rs),
    .Dest(dest_t), .D(d_t), .WE2(wEn), .Mem_out(Execute_mem_out), .target(Execute_target));
  // Probe on d_t
  Memory Memory (
    .WE(Ex_Mem_WE), .D(Ex_MEM_d_2), .Dest(Ex_Mem_Rd), .Mem_in(Ex_MEM_mem_2), .WE_2(Memory_we_2), .D_2(Mem_D),
    .M(Memory_m), .Dest_2(Memory_dest_2), .Mem_out(Memory_mem_out));
  EX_MEM Ex_MEM (
    .WE(wEn), .D(d_t), .Dest(dest_t), .Mem(Execute_mem_out), .target(Execute_target), .clk(Clock),
    .WE_2(Ex_Mem_WE), .D_2(Ex_MEM_d_2), .Dest_2(Ex_Mem_Rd), .Mem_2(Ex_MEM_mem_2));  // open: target_2
  MEM_WB MEM_WB (
    .WE(Memory_we_2), .D(Mem_D), .M(Memory_m), .Dest(Memory_dest_2), .Mem(Memory_mem_out), .clk(Clock),
    .WE_2(we_t), .D_2(MEM_WB_d_2), .M_2(m), .Dest_2(Dest), .Mem_2(Mem));
  // Probe on D
  Writeback WriteBack (.Dest(Dest), .D(MEM_WB_d_2), .M(m), .Mem(Mem), .WE(we_t), .rW(RD), .D_2(D), .WE_2(write));

  // Other names for the same wires on the sheet: clk = Clock
endmodule

module Immediate_Decode (
  input  IsR,
  input  [31:0] Op,
  output BorImmediate,
  output [31:0] Immediate
);

  wire and_1_out, and_2_out, and_3_out, not_1_out, not_2_out, not_3_out, not_4_out, not_5_out, or_1_out;
  wire [31:0] bit_extender_1_out, bit_extender_2_out;

  not not_1 (not_1_out, Op[26]);
  not not_2 (not_2_out, Op[28]);
  not not_3 (not_3_out, Op[30]);
  not not_4 (not_4_out, Op[26]);
  not not_5 (not_5_out, Op[28]);
  and and_1 (and_1_out, not_1_out, not_2_out, not_3_out);
  and and_2 (and_2_out, not_4_out, not_5_out, Op[29]);
  or or_1 (or_1_out, and_1_out, and_2_out);
  or or_2 (BorImmediate, or_1_out, IsR);
  and and_3 (and_3_out, Op[28], Op[29]);
  assign bit_extender_1_out = {{16{Op[15]}}, Op[15:0]};  // Bit_Extender bit_extender_1
  assign bit_extender_2_out = {{16{1'b0}}, Op[15:0]};  // Bit_Extender bit_extender_2
  Multiplexer #(.width(32), .enable("false")) multiplexer_1 (
    .in0(bit_extender_1_out), .in1(bit_extender_2_out), .out(Immediate), .sel(and_3_out));
endmodule

module Non_Immediate_Decode (
  input  [31:0] Op,
  output Enable,
  output whichSA,
  output [4:0] rd,
  output [4:0] rt,
  output [4:0] rs,
  output [3:0] Control,
  output Memory,
  output IsR
);

  wire and_4_out, Is_Branch, Is_JI, Is_JR;
  wire [3:0] rom_1_data, rom_2_data;

  and and_1 (Is_JI, ~Op[31], ~Op[30], ~Op[29], ~Op[28], Op[27]);  // AND_Gate
  nor nor_1 (Is_Branch, Op[29], IsR);
  and and_2 (Is_JR, ~Op[5], ~Op[4], Op[3], ~Op[2], ~Op[1]);  // AND_Gate
  and and_3 (IsR, ~Op[26], ~Op[27], ~Op[28], ~Op[29], ~Op[30], ~Op[31]);  // AND_Gate
  ROM #(.addrWidth(5), .dataWidth(4)) rom_1 (.addr({Op[31], Op[29:26]}), .data(rom_1_data));  // open: sel
  and and_4 (and_4_out, Is_JR, IsR);
  and and_5 (Enable, ~Op[31], ~Is_JI, ~Is_Branch, ~and_4_out);  // AND_Gate
  ROM #(.addrWidth(5), .dataWidth(4)) rom_2 (.addr({Op[5], Op[3:0]}), .data(rom_2_data));  // open: sel
  Multiplexer #(.width(4), .enable("false")) multiplexer_1 (
    .in0(rom_1_data), .in1(rom_2_data), .out(Control), .sel(IsR));

  assign Memory = Op[31];
  assign rd = Op[15:11];
  assign rs = Op[25:21];
  assign rt = Op[20:16];
  assign whichSA = Op[2];

  // Other names for the same wires on the sheet: Is_Mem = Op[31]

  // Notes on the sheet:
  //   contents of rom_1 (hex, n*v repeats v):
  //   0 d 0 0 9 b f d 0 2 f 7 8 a c 1 2 0 0 2 2 0 0 0 2 0 0 2
  //   contents of rom_2 (hex, n*v repeats v):
  //   0 0 4 5 0 0 4 5 0 0 9 b 5*0 2 0 6 8 a c e 0 0 f 7
endmodule

module Execute (
  input  [4:0] Rt,
  input  [31:0] A,
  input  [4:0] Rd,
  input  Is_R,
  input  [31:0] Mem_D,
  input  [31:0] WB_D,
  input  [3:0] ALU_Op,
  input  [31:0] Immediate,
  input  [31:0] B,
  input  whichSA,
  input  [4:0] ID_Ex_Ra,
  input  WE,
  input  Ex_Mem_WE,
  input  [4:0] Ex_Mem_Rd,
  input  B_or_Immediate,
  input  Mem_WB_WE,
  input  [4:0] Mem_WB_Rd,
  input  Mem_in,
  input  [31:0] PC_4,
  output [4:0] Dest,
  output [31:0] D,
  output WE2,
  output Mem_out,
  output [31:0] target
);

  wire ALU02, and_2_out, comparator_1_lt, eq_ne_cmd, eqzero_1_eqz, or_1_out, or_2_out, xor_1_out;
  wire [1:0] forwarding_unit_1_forward;
  wire [4:0] a_t, mips_alu_1_p4, multiplexer_4_out;
  wire [31:0] B_t, bit_extender_1_out, mips_alu_1_p5, multiplexer_3_out, multiplexer_6_out;
  wire [31:5] multiplexer_1_out;

  Multiplexer #(.select(2), .width(32), .enable("false")) multiplexer_1 (
    .in0(A), .in1(Mem_D), .in2(WB_D), .in3(A), .out({multiplexer_1_out, a_t}), .sel(forwarding_unit_1_forward));
  Multiplexer #(.select(2), .width(32), .enable("false")) multiplexer_2 (
    .in0(B), .in1(Mem_D), .in2(WB_D), .in3(B), .out(B_t), .sel(forwarding_unit_1_forward));
  Forwarding_Unit forwarding_unit_1 (
    .Ex_M_We(Ex_Mem_WE), .Ex_M_Rd(Ex_Mem_Rd), .ID_Ex_We(WE), .M_WB_We(Mem_WB_WE), .M_Wb_Rd(Mem_WB_Rd),
    .Id_Ex_Ra(ID_Ex_Ra), .Id_Ex_Rb(Rt), .BorImmediate(B_or_Immediate), .Forward(forwarding_unit_1_forward));
  Multiplexer #(.width(32), .enable("false")) multiplexer_3 (
    .in0(Immediate), .in1(B_t), .out(multiplexer_3_out), .sel(B_or_Immediate));
  Multiplexer #(.width(5), .enable("false")) multiplexer_4 (
    .in0(Immediate[10:6]), .in1(5'b10000), .out(multiplexer_4_out), .sel(ALU02));
  Comparator #(.width(32)) comparator_1 (
    .a({multiplexer_1_out, a_t}), .b(multiplexer_3_out), .lt(comparator_1_lt));  // open: gt, eq
  // Mips_ALU mips_alu_1: pin names not known; wires that end beside it: {multiplexer_1_out, a_t}, multiplexer_3_out, ALU_Op, mips_alu_1_p4, mips_alu_1_p5
  Multiplexer #(.width(5), .enable("false")) multiplexer_5 (
    .in0(multiplexer_4_out), .in1(a_t), .out(mips_alu_1_p4), .sel(whichSA));
  assign bit_extender_1_out = {{31{1'b0}}, comparator_1_lt};  // Bit_Extender bit_extender_1
  EqZero eqzero_1 (.A(B_t), .EqZ(eqzero_1_eqz));
  xor xor_1 (xor_1_out, eqzero_1_eqz, ALU_Op[1]);
  and and_1 (ALU02, ALU_Op[0], ~ALU_Op[2]);  // AND_Gate
  or or_1 (or_1_out, xor_1_out, ~eq_ne_cmd);  // OR_Gate
  and and_2 (and_2_out, ALU_Op[0], ALU_Op[1], ALU_Op[2]);
  and and_3 (eq_ne_cmd, ALU_Op[0], ~ALU_Op[2], ALU_Op[3]);  // AND_Gate
  Multiplexer #(.select(2), .width(32), .enable("false")) multiplexer_6 (
    .in0(mips_alu_1_p5), .in1(bit_extender_1_out), .in2({multiplexer_1_out, a_t}), .in3(bit_extender_1_out),
    .out(multiplexer_6_out), .sel(ALU_Op[3:2]));
  and and_4 (WE2, WE, or_1_out);
  or or_2 (or_2_out, eq_ne_cmd, and_2_out);
  Multiplexer #(.width(32), .enable("false")) multiplexer_7 (
    .in0(mips_alu_1_p5), .in1(multiplexer_6_out), .out(D), .sel(or_2_out));
  Multiplexer #(.width(5)) multiplexer_8 (.in0(Rt), .in1(Rd), .out(Dest), .sel(Is_R));  // open: en

  assign Mem_out = Mem_in;
  assign target = PC_4;

  // Other names for the same wires on the sheet: _2nd_bit = ALU_Op[1]; BorImmediate = B_or_Immediate;
  //   ID_Ex_Rb[4:0] = Rt; ID_Ex_WE = WE
endmodule

module Memory (
  input  WE,
  input  [31:0] D,
  input  [4:0] Dest,
  input  Mem_in,
  output WE_2,
  output [31:0] D_2,
  output [31:0] M,
  output [4:0] Dest_2,
  output Mem_out
);


  assign D_2 = D;
  assign Dest_2 = Dest;
  assign M = D;
  assign Mem_out = Mem_in;
  assign WE_2 = WE;
endmodule

module Writeback (
  input  [4:0] Dest,
  input  [31:0] D,
  input  [31:0] M,
  input  Mem,
  input  WE,
  output [4:0] rW,
  output [31:0] D_2,
  output WE_2
);

  Multiplexer #(.width(32)) multiplexer_1 (.in0(D), .in1(M), .out(D_2), .sel(Mem));  // open: en

  assign rW = Dest;
  assign WE_2 = WE;
endmodule

module IF_DE (
  input  [31:0] InstrIn,
  input  [31:0] PC_4,
  input  clk,
  output [31:0] Instr,
  output [31:0] PC_4_2
);

  Register #(.width(32)) register_1 (.D(InstrIn), .Q(Instr), .clk(clk));  // open: en, clr
  Register #(.width(32)) register_2 (.D(PC_4), .Q(PC_4_2), .clk(clk));  // open: en, clr
endmodule

module ID_EX (
  input  [4:0] Rs,
  input  [31:0] A,
  input  [31:0] B,
  input  WE,
  input  [4:0] Rt,
  input  [3:0] Op,
  input  [4:0] Rd,
  input  B_or_Immediate,
  input  [31:0] Imm,
  input  isR,
  input  Mem,
  input  [31:0] PC_4,
  input  whichSA,
  input  clk,
  output [4:0] Rs_2,
  output [31:0] A_2,
  output [31:0] B_2,
  output WE_2,
  output [4:0] Rt_2,
  output [3:0] Op_2,
  output [4:0] Rd_2,
  output B_or_Imm,
  output [31:0] Imm_2,
  output is_R,
  output Mem_2,
  output [31:0] PC_4_2,
  output whichSA_2
);

  Register #(.width(5)) u_Rs (.D(Rs), .Q(Rs_2), .clk(clk));  // open: en, clr
  Register #(.width(32)) u_A (.D(A), .Q(A_2), .clk(clk));  // open: en, clr
  Register #(.width(32)) u_B (.D(B), .Q(B_2), .clk(clk));  // open: en, clr
  D_Flip_Flop u_WE (.clk(clk), .D(WE), .Q(WE_2));  // open: Qn, preset, en, reset
  Register #(.width(5)) u_Rt (.D(Rt), .Q(Rt_2), .clk(clk));  // open: en, clr
  Register #(.width(4)) u_Op (.D(Op), .Q(Op_2), .clk(clk));  // open: en, clr
  Register #(.width(5)) u_Rd (.D(Rd), .Q(Rd_2), .clk(clk));  // open: en, clr
  Register #(.width(32)) u_Imm (.D(Imm), .Q(Imm_2), .clk(clk));  // open: en, clr
  Register #(.width(32)) register_1 (.D(PC_4), .Q(PC_4_2), .clk(clk));  // open: en, clr
  D_Flip_Flop u_B_or_immediate (.clk(clk), .D(B_or_Immediate), .Q(B_or_Imm));  // open: Qn, preset, en, reset
  D_Flip_Flop u_Is_R (.clk(clk), .D(isR), .Q(is_R));  // open: Qn, preset, en, reset
  D_Flip_Flop u_Mem (.clk(clk), .D(Mem), .Q(Mem_2));  // open: Qn, preset, en, reset
  D_Flip_Flop u_whichSA (.clk(clk), .D(whichSA), .Q(whichSA_2));  // open: Qn, preset, en, reset
endmodule

module EX_MEM (
  input  WE,
  input  [31:0] D,
  input  [4:0] Dest,
  input  Mem,
  input  [31:0] target,
  input  clk,
  output WE_2,
  output [31:0] D_2,
  output [4:0] Dest_2,
  output Mem_2,
  output [31:0] target_2
);

  Register #(.width(32)) u_D (.D(D), .Q(D_2), .clk(clk));  // open: en, clr
  Register #(.width(5)) u_Dest (.D(Dest), .Q(Dest_2), .clk(clk));  // open: en, clr
  Register #(.width(32)) register_1 (.D(target), .Q(target_2), .clk(clk));  // open: en, clr
  D_Flip_Flop u_WE (.clk(clk), .D(WE), .Q(WE_2));  // open: Qn, preset, en, reset
  D_Flip_Flop u_Mem (.clk(clk), .D(Mem), .Q(Mem_2));  // open: Qn, preset, en, reset
endmodule

module MEM_WB (
  input  WE,
  input  [31:0] D,
  input  [31:0] M,
  input  [4:0] Dest,
  input  Mem,
  input  clk,
  output WE_2,
  output [31:0] D_2,
  output [31:0] M_2,
  output [4:0] Dest_2,
  output Mem_2
);

  D_Flip_Flop #(.trigger("falling")) d_ff_1 (.clk(clk), .D(WE), .Q(WE_2));  // open: Qn, preset, en, reset
  Register #(.width(32)) register_1 (.D(D), .Q(D_2), .clk(clk));  // open: en, clr
  Register #(.width(32)) register_2 (.D(M), .Q(M_2), .clk(clk));  // open: en, clr
  Register #(.width(5)) register_3 (.D(Dest), .Q(Dest_2), .clk(clk));  // open: en, clr
  D_Flip_Flop d_ff_2 (.clk(clk), .D(Mem), .Q(Mem_2));  // open: Qn, preset, en, reset
endmodule

module EqZero (
  input  [31:0] A,
  output EqZ
);

  and and_1 (EqZ, ~A[0], ~A[1], ~A[2], ~A[3], ~A[4], ~A[5], ~A[6], ~A[7], ~A[8], ~A[9], ~A[10], ~A[11], ~A[12], ~A[13], ~A[14], ~A[15], ~A[16], ~A[17], ~A[18], ~A[19], ~A[20], ~A[21], ~A[22], ~A[23], ~A[24], ~A[25], ~A[26], ~A[27], ~A[28], ~A[29], ~A[30], ~A[31]);  // AND_Gate
endmodule

module Forwarding_Unit (
  input  [4:0] Id_Ex_Ra,
  input  [4:0] Id_Ex_Rb,
  input  Ex_M_We,
  input  [4:0] Ex_M_Rd,
  input  BorImmediate,
  input  ID_Ex_We,
  input  M_WB_We,
  input  [4:0] M_Wb_Rd,
  output [1:0] Forward
);

  wire and_1_out, and_2_out, ex_mem_bypass_1_forward, ex_mem_bypass_2_forward, mem_wb_bypass_1_forward,
       mem_wb_bypass_2_forward;

  Ex_Mem_Bypass ex_mem_bypass_1 (
    .Ex_M_We(Ex_M_We), .Ex_M_Rd(Ex_M_Rd), .Id_Ex_Ra_b(Id_Ex_Ra), .Forward(ex_mem_bypass_1_forward));
  Mem_WB_Bypass mem_wb_bypass_1 (
    .M_WB_WE(M_WB_We), .M_WB_Rd(M_Wb_Rd), .Id_Ex_Ra_b(Id_Ex_Ra), .ID_Ex_We(ID_Ex_We), .Ex_M_Rd(Ex_M_Rd),
    .Forward(mem_wb_bypass_1_forward));
  or or_1 (Forward[0], ex_mem_bypass_1_forward, and_2_out);
  or or_2 (Forward[1], mem_wb_bypass_1_forward, and_1_out);
  Ex_Mem_Bypass ex_mem_bypass_2 (
    .Ex_M_We(Ex_M_We), .Ex_M_Rd(Ex_M_Rd), .Id_Ex_Ra_b(Id_Ex_Rb), .Forward(ex_mem_bypass_2_forward));
  Mem_WB_Bypass mem_wb_bypass_2 (
    .M_WB_WE(M_WB_We), .M_WB_Rd(M_Wb_Rd), .Id_Ex_Ra_b(Id_Ex_Rb), .ID_Ex_We(ID_Ex_We), .Ex_M_Rd(Ex_M_Rd),
    .Forward(mem_wb_bypass_2_forward));
  and and_1 (and_1_out, mem_wb_bypass_2_forward, BorImmediate);
  and and_2 (and_2_out, ex_mem_bypass_2_forward, BorImmediate);
endmodule

module Ex_Mem_Bypass (
  input  Ex_M_We,
  input  [4:0] Ex_M_Rd,
  input  [4:0] Id_Ex_Ra_b,
  output Forward
);

  wire and_1_out, or_1_out;
  wire [4:0] not_1_out, xor_1_out;

  or or_1 (or_1_out, Ex_M_Rd[0], Ex_M_Rd[1], Ex_M_Rd[2], Ex_M_Rd[3], Ex_M_Rd[4]);
  assign not_1_out = ~xor_1_out;  // NOT_Gate not_1, 5 bits wide
  assign xor_1_out = Ex_M_Rd ^ Id_Ex_Ra_b;  // XOR_Gate xor_1, 5 bits wide
  and and_1 (and_1_out, not_1_out[0], not_1_out[1], not_1_out[2], not_1_out[3], not_1_out[4]);
  and and_2 (Forward, Ex_M_We, or_1_out, and_1_out);
endmodule

module Mem_WB_Bypass (
  input  M_WB_WE,
  input  [4:0] M_WB_Rd,
  input  [4:0] Id_Ex_Ra_b,
  input  ID_Ex_We,
  input  [4:0] Ex_M_Rd,
  output Forward
);

  wire ex_mem_bypass_1_forward, ex_mem_bypass_2_forward;

  Ex_Mem_Bypass ex_mem_bypass_1 (
    .Ex_M_We(M_WB_WE), .Ex_M_Rd(M_WB_Rd), .Id_Ex_Ra_b(Id_Ex_Ra_b), .Forward(ex_mem_bypass_1_forward));
  Ex_Mem_Bypass ex_mem_bypass_2 (
    .Ex_M_We(ID_Ex_We), .Ex_M_Rd(Ex_M_Rd), .Id_Ex_Ra_b(Id_Ex_Ra_b), .Forward(ex_mem_bypass_2_forward));
  and and_1 (Forward, ex_mem_bypass_1_forward, ~ex_mem_bypass_2_forward);  // AND_Gate
endmodule
